# Fritzing sketch PWM_generator_DC_motor (saved by Fritzing 0.9.3b)
breadboards: 1

parts:
  IC1 = General purpose bipolar Timer [package=dil-08]
  D1 = P1000K [part_number=1N4148]
  D2 = P1000K [part_number=1N4148]
  R1 = Rotary Potentiometer (Large) [maximum_resistance=50kΩ package=THT]
  R2 = Resistor [tolerance=±5% resistance=1k package="1206 [SMD]"]
  C1 = Electrolytic Capacitor [capacitance=0.1µF package="100 mil [THT, electrolytic]"]
  R3 = Resistor [tolerance=±5% resistance=220 package="1206 [SMD]"]
  M1 = DC Motor
  Q1 = MOSFET-NCHANNEL [package=to-92]
  VCC1 = Battery block 9V
  C2 = Ceramic Capacitor [capacitance=1nF package="0805 [SMD, multilayer]"]

nets:
  N1: IC1.GND, C1.-, Q1.S, VCC1.-, C2.1
  N2: IC1.TRI, IC1.TRE, R1.wiper, C1.+
  N3: IC1.OUT, R3.Pin_0
  N4: IC1._RES, IC1.VCC+, R2.Pin_0, M1.pin_1, VCC1.+
  N5: IC1.CON, C2.0
  N6: IC1.DIS, D1.cathode, D2.anode, R2.Pin_1
  N7: D1.anode, R1.leg1
  N8: D2.cathode, R1.leg2
  N9: R3.Pin_1, Q1.G
  N10: M1.pin_2, Q1.D

custom parts:
  MOSFET-NCHANNEL: Generic NMOS footprint
